// Logisim project Adder.circ as structural Verilog: 4 circuits, main circuit main
module main (
  input  [1:0] in_1,
  input  [1:0] in_2,
  output [2:0] out_3
);

  Adder adder_1 (.A1(in_1[1]), .A0(in_1[0]), .B1(in_2[1]), .B0(in_2[0]), .s3(out_3[2]), .s2(out_3[1]), .s1(out_3[0]));
endmodule

module Half_Adder (
  input  x,
  input  y,
  output s,
  output c
);

  xor xor_1 (s, x, y);
  and and_1 (c, x, y);
endmodule

module Full_Adder (
  input  A,
  input  B,
  input  C,
  output sum,
  output carry
);

  wire and_1_out, and_2_out, and_3_out, and_4_out, and_5_out, and_6_out, and_7_out, not_1_out, not_2_out,
       not_3_out, not_4_out, not_5_out, not_6_out;

  not not_1 (not_1_out, A);
  not not_2 (not_2_out, B);
  not not_3 (not_3_out, A);
  not not_4 (not_4_out, C);
  not not_5 (not_5_out, B);
  not not_6 (not_6_out, C);
  and and_1 (and_1_out, B, C);
  and and_2 (and_2_out, A, C);
  and and_3 (and_3_out, A, B);
  and and_4 (and_4_out, not_1_out, not_2_out, C);
  and and_5 (and_5_out, not_3_out, B, not_4_out);
  and and_6 (and_6_out, A, not_5_out, not_6_out);
  and and_7 (and_7_out, A, B, C);
  or or_1 (carry, and_1_out, and_2_out, and_3_out);
  or or_2 (sum, and_4_out, and_5_out, and_6_out, and_7_out);
endmodule

module Adder (
  input  A1,
  input  A0,
  input  B1,
  input  B0,
  output s3,
  output s2,
  output s1
);

  wire and_1_out, and_2_out, and_3_out, and_4_out, and_5_out, and_6_out, and_7_out, and_8_out, and_9_out,
       and_10_out, and_11_out, not_1_out, not_2_out, not_3_out, not_4_out, not_5_out, not_6_out, not_7_out,
       not_8_out, not_9_out, not_10_out, not_11_out, not_12_out;

  and and_1 (and_1_out, B1, A0, B0);
  and and_2 (and_2_out, A1, A0, B0);
  and and_3 (and_3_out, A1, B1);
  not not_1 (not_1_out, A1);
  not not_2 (not_2_out, A0);
  not not_3 (not_3_out, A1);
  not not_4 (not_4_out, B0);
  not not_5 (not_5_out, A1);
  not not_6 (not_6_out, B1);
  not not_7 (not_7_out, A0);
  not not_8 (not_8_out, B1);
  not not_9 (not_9_out, B1);
  not not_10 (not_10_out, B0);
  not not_11 (not_11_out, A0);
  and and_4 (and_4_out, not_11_out, B0);
  and and_5 (and_5_out, A0, not_12_out);
  not not_12 (not_12_out, B0);
  or or_1 (s3, and_1_out, and_2_out, and_3_out);
  and and_6 (and_6_out, not_1_out, not_2_out, B1);
  and and_7 (and_7_out, not_3_out, B1, not_4_out);
  and and_8 (and_8_out, not_5_out, A0, not_6_out, B0);
  and and_9 (and_9_out, A1, not_7_out, not_8_out);
  and and_10 (and_10_out, A1, not_9_out, not_10_out);
  and and_11 (and_11_out, A1, A0, B1, B0);
  or or_2 (s1, and_4_out, and_5_out);
  or or_3 (s2, and_6_out, and_7_out, and_8_out, and_9_out, and_10_out, and_11_out);
endmodule
